# Fritzing sketch sketch (saved by Fritzing 0.9.4)
breadboards: 1

parts:
  V1 = DC Power [voltage=12V]
  U1 = Voltage Regulator - 5V [package="TO220 [THT]"]
  WeMos_D1_Mini1 = WeMos D1 Mini
  Grove1 = Grove OLED 128x96
  U2 = PCF8574 [package="DIP16 [THT]"]

nets:
  N1: V1.V+, U1.input_voltage
  GND: V1.V-, U1.GND, WeMos_D1_Mini1.G, Grove1.GND, U2.A0, U2.A1, U2.A2, U2.GND
  VCC: U1.output_voltage, WeMos_D1_Mini1.5V, Grove1.VCC, U2.VCC
  N2: WeMos_D1_Mini1.D1, Grove1.SCL, U2.SDA
  N3: WeMos_D1_Mini1.D2, Grove1.SDA, U2.SCL
